# Fritzing sketch washerBuddy (saved by Fritzing 0.9.3b)
circuit board: 8.46667cm x 5.64444cm
breadboards: 1

parts:
  WeMos_D1_Mini1 = WeMos D1 Mini
  Water_detector = male pin header, 3 pins [form="♂ (male)"]
  Accelerometer = InvenSense MPU6050

nets:
  5V: WeMos_D1_Mini1.5V, Water_detector.pin3, Accelerometer.VCC
  N1: WeMos_D1_Mini1.D1, Accelerometer.SCL
  N2: WeMos_D1_Mini1.D2, Accelerometer.SDA
  N3: WeMos_D1_Mini1.D7, Water_detector.pin1
  N4: WeMos_D1_Mini1.G, Water_detector.pin2, Accelerometer.GND

custom parts:
  WeMos D1 Mini: The D1 mini is a mini wifi board based on ESP-8266EX.
